// Logisim project Circuito.circ as structural Verilog: 1 circuit, main circuit main
module main (
  input  A,
  input  B,
  input  C,
  output S
);

  wire and_1_out, nor_1_out, not_1_out, xor_1_out;

  not not_1 (not_1_out, B);
  nor nor_1 (nor_1_out, A, not_1_out, C);
  and and_1 (and_1_out, nor_1_out, B);
  xor xor_1 (xor_1_out, nor_1_out, and_1_out);
  not not_2 (S, xor_1_out);
endmodule
